# Fritzing sketch Untitled Sketch (saved by Fritzing 0.9.4)
circuit board: 8.46667cm x 5.64444cm
breadboards: 2

parts:
  IC1 = SHIFT REGISTER [package=dil16]
  IC2 = SHIFT REGISTER [package=dil16]
  IC3 = SHIFT REGISTER [package=dil16]
  U1 = ESP32S-HiLetgo [part_number=ESP32S-HiLetgo]
  Q1 = NPN-Transistor [package="TO92 [THT]"]
  LED1 = smd LED [color="Red (633nm)" package="0603 [SMD]"]  # not connected
  R2 = Resistor [tolerance=±5% resistance=470 package="1206 [SMD]"]
  R3 = Resistor [tolerance=±5% resistance=470 package="1206 [SMD]"]
  R4 = Resistor [tolerance=±5% resistance=470 package="1206 [SMD]"]
  R5 = Resistor [tolerance=±5% resistance=470 package="1206 [SMD]"]
  LED3 = smd LED [color="Red (633nm)" package="0603 [SMD]"]
  LED4 = smd LED [color="Red (633nm)" package="0603 [SMD]"]
  LED5 = smd LED [color="Red (633nm)" package="0603 [SMD]"]
  V1 = DC Power [voltage=5]
  R6 = Resistor [tolerance=±5% resistance=470 package="1206 [SMD]"]
  R7 = Resistor [tolerance=±5% resistance=470 package="1206 [SMD]"]
  R8 = Resistor [tolerance=±5% resistance=470 package="1206 [SMD]"]
  R9 = Resistor [tolerance=±5% resistance=470 package="1206 [SMD]"]
  R10 = Resistor [tolerance=±5% resistance=470 package="1206 [SMD]"]
  R11 = Resistor [tolerance=±5% resistance=470 package="1206 [SMD]"]
  R12 = Resistor [tolerance=±5% resistance=470 package="1206 [SMD]"]
  R13 = Resistor [tolerance=±5% resistance=470 package="1206 [SMD]"]
  R14 = Resistor [tolerance=±5% resistance=470 package="1206 [SMD]"]
  R15 = Resistor [tolerance=±5% resistance=470 package="1206 [SMD]"]
  R16 = Resistor [tolerance=±5% resistance=470 package="1206 [SMD]"]
  R17 = Resistor [tolerance=±5% resistance=470 package="1206 [SMD]"]
  R18 = Resistor [tolerance=±5% resistance=470 package="1206 [SMD]"]
  R19 = Resistor [tolerance=±5% resistance=470 package="1206 [SMD]"]
  R20 = Resistor [tolerance=±5% resistance=470 package="1206 [SMD]"]
  R21 = Resistor [tolerance=±5% resistance=470 package="1206 [SMD]"]
  R22 = Resistor [tolerance=±5% resistance=470 package="1206 [SMD]"]
  R23 = Resistor [tolerance=±5% resistance=470 package="1206 [SMD]"]
  R24 = Resistor [tolerance=±5% resistance=470 package="1206 [SMD]"]
  R25 = Resistor [tolerance=±5% resistance=470 package="1206 [SMD]"]
  LED6 = smd LED [color="Red (633nm)" package="0603 [SMD]"]
  LED7 = smd LED [color="Red (633nm)" package="0603 [SMD]"]
  LED8 = smd LED [color="Red (633nm)" package="0603 [SMD]"]
  LED9 = smd LED [color="Red (633nm)" package="0603 [SMD]"]
  LED10 = smd LED [color="Red (633nm)" package="0603 [SMD]"]
  LED11 = smd LED [color="Red (633nm)" package="0603 [SMD]"]
  LED12 = smd LED [color="Red (633nm)" package="0603 [SMD]"]
  LED13 = smd LED [color="Red (633nm)" package="0603 [SMD]"]
  LED14 = smd LED [color="Red (633nm)" package="0603 [SMD]"]
  LED15 = smd LED [color="Red (633nm)" package="0603 [SMD]"]
  LED16 = smd LED [color="Red (633nm)" package="0603 [SMD]"]
  LED17 = smd LED [color="Red (633nm)" package="0603 [SMD]"]
  LED18 = smd LED [color="Red (633nm)" package="0603 [SMD]"]
  LED19 = smd LED [color="Red (633nm)" package="0603 [SMD]"]
  LED20 = smd LED [color="Red (633nm)" package="0603 [SMD]"]
  LED21 = smd LED [color="Red (633nm)" package="0603 [SMD]"]
  LED22 = smd LED [color="Red (633nm)" package="0603 [SMD]"]
  LED23 = smd LED [color="Red (633nm)" package="0603 [SMD]"]
  LED24 = smd LED [color="Red (633nm)" package="0603 [SMD]"]
  LED25 = smd LED [color="Red (633nm)" package="0603 [SMD]"]
  IC4 = SHIFT REGISTER [package=dil16]
  R26 = Resistor [tolerance=±5% resistance=470 package="1206 [SMD]"]
  R27 = Resistor [tolerance=±5% resistance=470 package="1206 [SMD]"]
  R28 = Resistor [tolerance=±5% resistance=470 package="1206 [SMD]"]
  R29 = Resistor [tolerance=±5% resistance=470 package="1206 [SMD]"]
  R30 = Resistor [tolerance=±5% resistance=470 package="1206 [SMD]"]
  R31 = Resistor [tolerance=±5% resistance=470 package="1206 [SMD]"]
  R32 = Resistor [tolerance=±5% resistance=470 package="1206 [SMD]"]
  R33 = Resistor [tolerance=±5% resistance=470 package="1206 [SMD]"]
  LED26 = smd LED [color="Red (633nm)" package="0603 [SMD]"]
  LED27 = smd LED [color="Red (633nm)" package="0603 [SMD]"]
  LED28 = smd LED [color="Red (633nm)" package="0603 [SMD]"]
  LED29 = smd LED [color="Red (633nm)" package="0603 [SMD]"]
  LED30 = smd LED [color="Red (633nm)" package="0603 [SMD]"]
  LED31 = smd LED [color="Red (633nm)" package="0603 [SMD]"]
  LED32 = smd LED [color="Red (633nm)" package="0603 [SMD]"]
  LED33 = smd LED [color="Red (633nm)" package="0603 [SMD]"]
  R34 = Photocell (LDR) [package=THT]
  R35 = Resistor [tolerance=±5% resistance=220 package="2010 [SMD]"]

nets:
  N1: IC1.QB, R3.Pin_1
  N2: IC1.QC, R4.Pin_1
  N3: IC1.QD, R5.Pin_1
  N4: IC1.QE, R6.Pin_1
  N5: IC1.QF, R25.Pin_1
  N6: IC1.QG, R24.Pin_1
  N7: IC1.QH, R23.Pin_1
  GND: IC1.GND, IC1.G, IC2.GND, IC2.G, IC3.GND, IC3.G, U1.GND, Q1.E, V1.V-, IC4.GND, IC4.G, R34.pin_1
  N8: IC1.QH*, IC2.SER
  VCC: IC1.SCL, IC1.VCC, IC2.SCL, IC2.VCC, IC3.SCL, IC3.VCC, U1.VIN, V1.V+, IC4.SCL, IC4.VCC, R35.Pin_0
  N9: IC1.SCK, IC2.SCK, IC3.SCK, U1.GPIO4, IC4.SCK
  N10: IC1.RCK, IC2.RCK, IC3.RCK, U1.GPIO2, IC4.RCK
  N11: IC1.SER, U1.GPIO15
  N12: IC1.QA, R2.Pin_1
  N13: IC2.QB, R7.Pin_1
  N14: IC2.QC, R21.Pin_1
  N15: IC2.QD, R20.Pin_1
  N16: IC2.QE, R19.Pin_1
  N17: IC2.QF, R18.Pin_1
  N18: IC2.QG, R17.Pin_1
  N19: IC2.QH, R16.Pin_1
  N20: IC2.QH*, IC3.SER
  N21: IC2.QA, R22.Pin_1
  N22: IC3.QB, R15.Pin_1
  N23: IC3.QC, R14.Pin_1
  N24: IC3.QD, R12.Pin_1
  N25: IC3.QE, R11.Pin_1
  N26: IC3.QF, R10.Pin_1
  N27: IC3.QG, R9.Pin_1
  N28: IC3.QH, R8.Pin_1
  N29: IC3.QH*, IC4.SER
  N30: IC3.QA, R13.Pin_1
  N31: U1.GPIO12, Q1.B
  N32: U1.GPIO3, R34.pin_0, R35.Pin_1
  N33: Q1.C, R2.Pin_0, R3.Pin_0, LED3.cathode, LED4.anode, LED5.anode, LED6.cathode, LED7.cathode, LED8.cathode, LED9.cathode, LED10.cathode, LED11.cathode, LED12.cathode, LED13.cathode, LED14.cathode, LED15.cathode, LED16.cathode, LED17.cathode, LED18.cathode, LED19.cathode, LED20.cathode, LED21.cathode, LED22.cathode, LED23.cathode, LED24.cathode, LED25.cathode, LED26.cathode, LED27.cathode, LED28.cathode, LED29.cathode, LED30.cathode, LED31.cathode, LED32.cathode, LED33.cathode
  N34: R6.Pin_0, LED25.anode
  N35: R7.Pin_0, LED20.anode
  N36: R8.Pin_0, LED6.anode
  N37: R9.Pin_0, LED7.anode
  N38: R10.Pin_0, LED8.anode
  N39: R11.Pin_0, LED9.anode
  N40: R12.Pin_0, LED10.anode
  N41: R13.Pin_0, LED13.anode
  N42: R14.Pin_0, LED11.anode
  N43: R15.Pin_0, LED12.anode
  N44: R16.Pin_0, LED14.anode
  N45: R17.Pin_0, LED15.anode
  N46: R18.Pin_0, LED16.anode
  N47: R19.Pin_0, LED17.anode
  N48: R20.Pin_0, LED18.anode
  N49: R21.Pin_0, LED19.anode
  N50: R22.Pin_0, LED21.anode
  N51: R23.Pin_0, LED22.anode
  N52: R24.Pin_0, LED23.anode
  N53: R25.Pin_0, LED24.anode
  N54: IC4.QB, R31.Pin_1
  N55: IC4.QC, R30.Pin_1
  N56: IC4.QD, R29.Pin_1
  N57: IC4.QE, R28.Pin_1
  N58: IC4.QF, R27.Pin_1
  N59: IC4.QG, R33.Pin_1
  N60: IC4.QH, R26.Pin_1
  N61: IC4.QA, R32.Pin_1
  N62: R26.Pin_0, LED26.anode
  N63: R27.Pin_0, LED28.anode
  N64: R28.Pin_0, LED29.anode
  N65: R29.Pin_0, LED30.anode
  N66: R30.Pin_0, LED31.anode
  N67: R31.Pin_0, LED32.anode
  N68: R32.Pin_0, LED33.anode
  N69: R33.Pin_0, LED27.anode

custom parts:
  ESP32S-HiLetgo: HiLetgo ESP-WROOM-32 ESP32 ESP-32S Development Board 2.4GHz Dual-Mode WiFi + Bluetooth Dual Cores Microcontroller The ESP32 integrated with Antenna switches, RF Balun, power amplifiers, low-noise amplifiers, filters, and management modules, and the entire solution occupies the least area of PCB. 2.4 GHz Wi-Fi plus Bluetooth dual-mode chip, with TSMC Ultra-low power consumption 40nm technology,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

// code stored in the sketch: Untitled.ino
/*
  74HC595 Shift Register Demonstration 1
  74hc595-demo.ino
  Count in Binary and display on 8 LEDs

  Modified from "Hello World" example by Carlyn Maw,Tom Igoe and David A. Mellis

  DroneBot Workshop 2020
  https://dronebotworkshop.com
*/

// the number of the LED pin
const int ledPin = 13; // 16 corresponds to GPIO16

// setting PWM properties
const int freq = 5000;
const int ledChannel = 0;
const int resolution = 8;

// Define Connections to 74HC595

// ST_CP pin 12
const int latchPin = 2;
// SH_CP pin 11
const int clockPin = 4;
// DS pin 14
const int dataPin = 15;

const int blink[] {1,2,4,8,16,32,64,128};
//const int blink1[] {9,18,36,72,144,72,36,18};
//const int marquee[] {170, 85} ;
void setup ()
{

  // Setup pins as Outputs
  pinMode(latchPin, OUTPUT);
  pinMode(clockPin, OUTPUT);
  pinMode(dataPin, OUTPUT);
ledcSetup(ledChannel, freq, resolution);
ledcAttachPin(ledPin, ledChannel);

}

  int d = 112;
void loop() {
//  int rn = 255;
//  int a = random(1, rn);
//  int b = random(1, rn);
//  int c = random(1, rn);
//          int a = 255;
//          int b = 255;
//          int c = 255;
  // ST_CP LOW to keep LEDs from changing while reading serial data
ledcWrite(ledChannel, d);
for(int b:blink){
    digitalWrite(latchPin, LOW);

    shiftOut(dataPin, clockPin, MSBFIRST, b);

    shiftOut(dataPin, clockPin, MSBFIRST, b);
    
    shiftOut(dataPin, clockPin, MSBFIRST, b);
    
    digitalWrite(latchPin, HIGH);
    delay(100);
}
    d= (d<16)*112 + (d>=16)*(d-8);

}
